// Digital circuit maquina de moore 1.dig as structural Verilog
module maquina_de_moore_1 (
  input  clk,
  input  in_2,
  input  in_3
);

  wire and_1_out, and_2_out, and_3_out, and_4_out, d_ff_1_nq, d_ff_1_q, d_ff_2_q, or_1_out, or_2_out;

  and and_1 (and_1_out, in_2, in_3, d_ff_1_q);
  and and_2 (and_2_out, in_2, in_3, d_ff_1_nq);
  and and_3 (and_3_out, in_3, d_ff_1_nq, d_ff_2_q);
  and and_4 (and_4_out, in_3, d_ff_1_nq, d_ff_2_q);
  or or_1 (or_1_out, and_1_out, and_2_out);
  or or_2 (or_2_out, and_3_out, and_4_out);
  D_FF d_ff_1 (.D(or_1_out), .C(clk), .Q(d_ff_1_q), .nQ(d_ff_1_nq));
  D_FF d_ff_2 (.D(or_2_out), .C(clk), .Q(d_ff_2_q));  // open: nQ
  LED led_1 (.in(d_ff_2_q));
  LED led_2 (.in(d_ff_1_q));
endmodule
