// Digital circuit questão 1 prática 2.dig as structural Verilog
module \questão_1_prática_2  (
  input  A1,
  input  A2,
  input  A3,
  input  A4,
  input  A5,
  input  A6,
  input  A7,
  input  B1,
  input  B2,
  input  B3,
  input  B4,
  input  B5,
  input  B6,
  input  B7
);

  wire _74283_1_pin1, _74283_1_pin4, _74283_1_pin9, _74283_1_pin10, _74283_1_pin13, _74283_2_pin1,
       _74283_2_pin4, _74283_2_pin9, _74283_2_pin10, _74283_2_pin13;

  _74283 _74283_1 (
    .pin1(_74283_1_pin1), .pin2(B2), .pin3(A2), .pin4(_74283_1_pin4), .pin5(A1), .pin6(B1), .pin7(1'b0),
    .pin8(1'b0), .pin9(_74283_1_pin9), .pin10(_74283_1_pin10), .pin11(B4), .pin12(A4),
    .pin13(_74283_1_pin13), .pin14(A3), .pin15(B3), .pin16(1'b1));
  _74283 _74283_2 (
    .pin1(_74283_2_pin1), .pin2(B6), .pin3(A6), .pin4(_74283_2_pin4), .pin5(A5), .pin6(B5),
    .pin7(_74283_1_pin9), .pin8(1'b0), .pin9(_74283_2_pin9), .pin10(_74283_2_pin10), .pin11(1'b0),
    .pin12(1'b0), .pin13(_74283_2_pin13), .pin14(A7), .pin15(B7), .pin16(1'b1));
  LED S9 (.in(_74283_2_pin9));
  LED S8__c_out (.in(_74283_2_pin10));
  LED S6 (.in(_74283_2_pin1));
  LED S7 (.in(_74283_2_pin13));
  LED S4 (.in(_74283_1_pin10));
  LED S5 (.in(_74283_2_pin4));
  LED S2 (.in(_74283_1_pin1));
  LED S3 (.in(_74283_1_pin13));
  LED S1 (.in(_74283_1_pin4));

  // Notes on the sheet:
  //   // Questão 1 - cicuito somador de 14 bits
endmodule
