// Digital circuit questão 1prática 3 MEF.dig as structural Verilog
module \questão_1prática_3_MEF  (
  input  clk,
  input  in_2
);

  wire and_1_out, and_2_out, and_3_out, and_4_out, and_5_out, and_6_out, nQ0, nQ1, nQ2, or_1_out, or_2_out,
       or_3_out, Q0, Q1, Q2;

  and and_1 (and_1_out, nQ0, nQ2);
  and and_2 (and_2_out, Q2, Q0);
  and and_3 (and_3_out, nQ0, nQ2);
  and and_4 (and_4_out, Q2, nQ1, Q0);
  and and_5 (and_5_out, nQ2, nQ1);
  and and_6 (and_6_out, Q2, Q1);
  or or_1 (or_1_out, and_1_out, and_2_out, Q1);
  or or_2 (or_2_out, and_3_out, and_4_out);
  or or_3 (or_3_out, and_5_out, and_6_out);
  D_FF_AS d_ff_as_1 (.Set(in_2), .D(or_1_out), .C(clk), .Clr(in_2), .Q(Q0), .nQ(nQ0));
  D_FF_AS d_ff_as_2 (.Set(in_2), .D(or_2_out), .C(clk), .Clr(in_2), .Q(Q1), .nQ(nQ1));
  D_FF_AS d_ff_as_3 (.Set(in_2), .D(or_3_out), .C(clk), .Clr(in_2), .Q(Q2), .nQ(nQ2));
  Seven_Seg_Hex seven_seg_hex_1 (.d({1'b0, Q2, Q1, Q0}), .dp(1'b0));
endmodule
