// Digital circuit questão 2- relógio pratica 3.dig as structural Verilog
module \questão_2__relógio_pratica_3  (
  input  clk,
  input  Start___Pause
);

  wire _0, _1, _2, _3, _4, _5, _6, _7, _8, _9, _10, _11, _12, _13, _14, _15, _16, _17, _18, _19, _20, _21,
       _22, _23, _24, _25, _26, _27, _28, _29, _30, _31, _32, _33, _34, _35, _36, _37, _38, _39, _40, _41,
       and_1_out, and_2_out, and_3_out, and_4_out, and_5_out, and_6_out, jk_ff_as_1_nq, jk_ff_as_2_nq,
       jk_ff_as_3_nq, jk_ff_as_5_nq, jk_ff_as_6_nq, jk_ff_as_8_nq, jk_ff_as_9_nq, jk_ff_as_10_nq,
       jk_ff_as_12_nq, jk_ff_as_13_nq, jk_ff_as_15_nq, jk_ff_as_16_nq, jk_ff_as_17_nq, jk_ff_as_19_nq,
       not_1_out, not_2_out, not_3_out, not_4_out, not_5_out, not_6_out, not_7_out, not_8_out, not_9_out,
       not_10_out, not_11_out, or_1_out, Q0, Q1, Q2, Q3, Q4, Q5, Q6, Q7, Q8, Q9, Q10, Q11, Q12, Q13, Q14,
       Q15, Q16, Q17, Q18, Q19;

  JK_FF_AS jk_ff_as_1 (
    .Set(1'b0), .J(Start___Pause), .C(clk), .K(Start___Pause), .Clr(and_1_out), .Q(Q0), .nQ(jk_ff_as_1_nq));
  and and_1 (and_1_out, Q3, not_2_out, Q1, not_1_out);
  not not_1 (not_1_out, Q0);
  not not_2 (not_2_out, Q2);
  JK_FF_AS jk_ff_as_2 (
    .Set(1'b0), .J(Start___Pause), .C(jk_ff_as_1_nq), .K(Start___Pause), .Clr(and_1_out), .Q(Q1),
    .nQ(jk_ff_as_2_nq));
  _7448 _7448_1 (
    .pin1(Q1), .pin2(Q2), .pin3(1'b1), .pin4(1'b1), .pin5(1'b1), .pin6(Q3), .pin7(Q0), .pin8(1'b0),
    .pin9(_4), .pin10(_3), .pin11(_2), .pin12(_1), .pin13(_0), .pin14(_6), .pin15(_5), .pin16(1'b1));
  JK_FF_AS jk_ff_as_3 (
    .Set(1'b0), .J(Start___Pause), .C(jk_ff_as_2_nq), .K(Start___Pause), .Clr(and_1_out), .Q(Q2),
    .nQ(jk_ff_as_3_nq));
  JK_FF_AS jk_ff_as_4 (
    .Set(1'b0), .J(Start___Pause), .C(jk_ff_as_3_nq), .K(Start___Pause), .Clr(and_1_out), .Q(Q3));  // open: nQ
  JK_FF_AS jk_ff_as_5 (
    .Set(1'b0), .J(Start___Pause), .C(and_1_out), .K(Start___Pause), .Clr(and_2_out), .Q(Q4),
    .nQ(jk_ff_as_5_nq));
  and and_2 (and_2_out, Q6, Q5, not_3_out);
  JK_FF_AS jk_ff_as_6 (
    .Set(1'b0), .J(Start___Pause), .C(jk_ff_as_5_nq), .K(Start___Pause), .Clr(and_2_out), .Q(Q5),
    .nQ(jk_ff_as_6_nq));
  not not_3 (not_3_out, Q4);
  _7448 _7448_2 (
    .pin1(Q5), .pin2(Q6), .pin3(1'b1), .pin4(1'b1), .pin5(1'b1), .pin6(1'b0), .pin7(Q4), .pin8(1'b0),
    .pin9(_11), .pin10(_10), .pin11(_9), .pin12(_8), .pin13(_7), .pin14(_13), .pin15(_12), .pin16(1'b1));
  JK_FF_AS jk_ff_as_7 (
    .Set(1'b0), .J(Start___Pause), .C(jk_ff_as_6_nq), .K(Start___Pause), .Clr(and_2_out), .Q(Q6));  // open: nQ
  Seven_Seg seven_seg_1 (.a(_35), .b(_36), .c(_37), .d(_38), .e(_39), .f(_40), .g(_41), .dp(1'b0));
  JK_FF_AS jk_ff_as_8 (
    .Set(1'b0), .J(Start___Pause), .C(and_2_out), .K(Start___Pause), .Clr(and_3_out), .Q(Q7),
    .nQ(jk_ff_as_8_nq));
  and and_3 (and_3_out, Q10, not_5_out, Q8, not_4_out);
  Seven_Seg seven_seg_2 (.a(_28), .b(_29), .c(_30), .d(_31), .e(_32), .f(_33), .g(_34), .dp(1'b0));
  not not_4 (not_4_out, Q7);
  not not_5 (not_5_out, Q9);
  JK_FF_AS jk_ff_as_9 (
    .Set(1'b0), .J(Start___Pause), .C(jk_ff_as_8_nq), .K(Start___Pause), .Clr(and_3_out), .Q(Q8),
    .nQ(jk_ff_as_9_nq));
  Seven_Seg seven_seg_3 (.a(_21), .b(_22), .c(_23), .d(_24), .e(_25), .f(_26), .g(_27), .dp(1'b0));
  _7448 _7448_3 (
    .pin1(Q8), .pin2(Q9), .pin3(1'b1), .pin4(1'b1), .pin5(1'b1), .pin6(Q10), .pin7(Q7), .pin8(1'b0),
    .pin9(_18), .pin10(_17), .pin11(_16), .pin12(_15), .pin13(_14), .pin14(_20), .pin15(_19), .pin16(1'b1));
  Seven_Seg seven_seg_4 (.a(_14), .b(_15), .c(_16), .d(_17), .e(_18), .f(_19), .g(_20), .dp(1'b0));
  JK_FF_AS jk_ff_as_10 (
    .Set(1'b0), .J(Start___Pause), .C(jk_ff_as_9_nq), .K(Start___Pause), .Clr(and_3_out), .Q(Q9),
    .nQ(jk_ff_as_10_nq));
  Seven_Seg seven_seg_5 (.a(_7), .b(_8), .c(_9), .d(_10), .e(_11), .f(_12), .g(_13), .dp(1'b0));
  JK_FF_AS jk_ff_as_11 (
    .Set(1'b0), .J(Start___Pause), .C(jk_ff_as_10_nq), .K(Start___Pause), .Clr(and_3_out), .Q(Q10));  // open: nQ
  Seven_Seg seven_seg_6 (.a(_0), .b(_1), .c(_2), .d(_3), .e(_4), .f(_5), .g(_6), .dp(1'b0));
  JK_FF_AS jk_ff_as_12 (
    .Set(1'b0), .J(Start___Pause), .C(and_3_out), .K(Start___Pause), .Clr(and_4_out), .Q(Q11),
    .nQ(jk_ff_as_12_nq));
  not not_6 (not_6_out, Q11);
  and and_4 (and_4_out, Q13, Q12, not_6_out);
  JK_FF_AS jk_ff_as_13 (
    .Set(1'b0), .J(Start___Pause), .C(jk_ff_as_12_nq), .K(Start___Pause), .Clr(and_4_out), .Q(Q12),
    .nQ(jk_ff_as_13_nq));
  _7448 _7448_4 (
    .pin1(Q12), .pin2(Q13), .pin3(1'b1), .pin4(1'b1), .pin5(1'b1), .pin6(1'b0), .pin7(Q11), .pin8(1'b0),
    .pin9(_25), .pin10(_24), .pin11(_23), .pin12(_22), .pin13(_21), .pin14(_27), .pin15(_26), .pin16(1'b1));
  JK_FF_AS jk_ff_as_14 (
    .Set(1'b0), .J(Start___Pause), .C(jk_ff_as_13_nq), .K(Start___Pause), .Clr(and_4_out), .Q(Q13));  // open: nQ
  JK_FF_AS jk_ff_as_15 (
    .Set(1'b0), .J(Start___Pause), .C(and_4_out), .K(Start___Pause), .Clr(or_1_out), .Q(Q14),
    .nQ(jk_ff_as_15_nq));
  or or_1 (or_1_out, and_6_out, and_5_out);
  JK_FF_AS jk_ff_as_16 (
    .Set(1'b0), .J(Start___Pause), .C(jk_ff_as_15_nq), .K(Start___Pause), .Clr(or_1_out), .Q(Q15),
    .nQ(jk_ff_as_16_nq));
  and and_5 (and_5_out, Q17, not_8_out, Q15, not_7_out);
  not not_7 (not_7_out, Q14);
  not not_8 (not_8_out, Q16);
  JK_FF_AS jk_ff_as_17 (
    .Set(1'b0), .J(Start___Pause), .C(jk_ff_as_16_nq), .K(Start___Pause), .Clr(or_1_out), .Q(Q16),
    .nQ(jk_ff_as_17_nq));
  _7448 _7448_5 (
    .pin1(Q15), .pin2(Q16), .pin3(1'b1), .pin4(1'b1), .pin5(1'b1), .pin6(Q17), .pin7(Q14), .pin8(1'b0),
    .pin9(_32), .pin10(_31), .pin11(_30), .pin12(_29), .pin13(_28), .pin14(_34), .pin15(_33), .pin16(1'b1));
  JK_FF_AS jk_ff_as_18 (
    .Set(1'b0), .J(Start___Pause), .C(jk_ff_as_17_nq), .K(Start___Pause), .Clr(or_1_out), .Q(Q17));  // open: nQ
  JK_FF_AS jk_ff_as_19 (
    .Set(1'b0), .J(Start___Pause), .C(or_1_out), .K(Start___Pause), .Clr(and_6_out), .Q(Q18),
    .nQ(jk_ff_as_19_nq));
  and and_6 (and_6_out, Q19, not_11_out, Q16, not_10_out, not_9_out);
  JK_FF_AS jk_ff_as_20 (
    .Set(1'b0), .J(Start___Pause), .C(jk_ff_as_19_nq), .K(Start___Pause), .Clr(and_6_out), .Q(Q19));  // open: nQ
  not not_9 (not_9_out, Q14);
  not not_10 (not_10_out, Q15);
  not not_11 (not_11_out, Q18);
  _7448 _7448_6 (
    .pin1(Q19), .pin2(1'b0), .pin3(1'b1), .pin4(1'b1), .pin5(1'b1), .pin6(1'b0), .pin7(Q18), .pin8(1'b0),
    .pin9(_39), .pin10(_38), .pin11(_37), .pin12(_36), .pin13(_35), .pin14(_41), .pin15(_40), .pin16(1'b1));

  // Notes on the sheet:
  //   clk: Hz: 7000
  //   HORAS
  //   MINUTOS
  //   SEGUNDOS
endmodule
