// Digital circuit questão 2. pratica 2 .dig as structural Verilog
module \questão_2__pratica_2  (
  input  A_1,
  input  A_2,
  input  A_3,
  input  A_4,
  input  B_1,
  input  B_2,
  input  B_3,
  input  B_4,
  input  in_12,
  output out_9,
  output out_10,
  output OVERFLOW
);

  wire _7448_1_pin9, _7448_1_pin10, _7448_1_pin11, _7448_1_pin12, _7448_1_pin13, _7448_1_pin14,
       _7448_1_pin15, and_3_out, and_5_out, and_6_out, and_7_out, and_8_out, and_9_out, and_10_out,
       and_11_out, and_12_out, and_13_out, and_14_out, and_15_out, and_16_out, not_1_out, not_2_out,
       not_3_out, not_4_out, or_1_out, or_2_out, or_3_out, xor_5_out, xor_6_out, xor_7_out, xor_8_out,
       xor_9_out, xor_10_out, xor_11_out, xor_12_out;
  wire [4:0] multiplexer_1_out, xor_1_out;

  not not_1 (not_1_out, B_4);
  not not_2 (not_2_out, B_2);
  not not_3 (not_3_out, B_3);
  not not_4 (not_4_out, B_1);
  xor xor_1 (xor_1_out[0], not_4_out, 1'b1);
  and and_1 (out_9, 1'b1, not_4_out);
  xor xor_2 (xor_1_out[1], out_9, not_2_out);
  and and_2 (out_10, out_9, not_2_out);
  xor xor_3 (xor_1_out[2], out_10, not_3_out);
  and and_3 (and_3_out, out_10, not_3_out);
  xor xor_4 (xor_1_out[3], and_3_out, not_1_out);
  and and_4 (xor_1_out[4], and_3_out, not_1_out);
  Multiplexer #(.Bits(5)) multiplexer_1 (
    .sel(B_4), .in_0({1'b0, B_4, B_3, B_2, B_1}), .in_1(xor_1_out), .out(multiplexer_1_out));
  xor xor_5 (xor_5_out, A_1, multiplexer_1_out[0]);
  and and_5 (and_5_out, multiplexer_1_out[0], A_1);
  and and_6 (and_6_out, multiplexer_1_out[4], A_1);
  and and_7 (and_7_out, multiplexer_1_out[4], multiplexer_1_out[0]);
  xor xor_6 (xor_6_out, xor_5_out, multiplexer_1_out[4]);
  or or_1 (or_1_out, and_5_out, and_6_out, and_7_out);
  xor xor_7 (xor_7_out, A_2, multiplexer_1_out[1]);
  and and_8 (and_8_out, multiplexer_1_out[1], A_2);
  and and_9 (and_9_out, or_1_out, A_2);
  and and_10 (and_10_out, or_1_out, multiplexer_1_out[1]);
  xor xor_8 (xor_8_out, xor_7_out, or_1_out);
  or or_2 (or_2_out, and_8_out, and_9_out, and_10_out);
  xor xor_9 (xor_9_out, A_3, multiplexer_1_out[2]);
  and and_11 (and_11_out, multiplexer_1_out[2], A_3);
  and and_12 (and_12_out, or_2_out, A_3);
  and and_13 (and_13_out, or_2_out, multiplexer_1_out[2]);
  xor xor_10 (xor_10_out, xor_9_out, or_2_out);
  or or_3 (or_3_out, and_11_out, and_12_out, and_13_out);
  xor xor_11 (xor_11_out, A_4, multiplexer_1_out[3]);
  and and_14 (and_14_out, multiplexer_1_out[3], A_4);
  and and_15 (and_15_out, or_3_out, A_4);
  and and_16 (and_16_out, or_3_out, multiplexer_1_out[3]);
  xor xor_12 (xor_12_out, xor_11_out, or_3_out);
  or or_4 (OVERFLOW, and_14_out, and_15_out, and_16_out);
  _7448 _7448_1 (
    .pin1(xor_8_out), .pin2(xor_10_out), .pin3(in_12), .pin4(in_12), .pin5(in_12), .pin6(xor_12_out),
    .pin7(xor_6_out), .pin8(1'b0), .pin9(_7448_1_pin9), .pin10(_7448_1_pin10), .pin11(_7448_1_pin11),
    .pin12(_7448_1_pin12), .pin13(_7448_1_pin13), .pin14(_7448_1_pin14), .pin15(_7448_1_pin15), .pin16(1'b1));
  Seven_Seg seven_seg_1 (
    .a(_7448_1_pin13), .b(_7448_1_pin12), .c(_7448_1_pin11), .d(_7448_1_pin10), .e(_7448_1_pin9),
    .f(_7448_1_pin15), .g(_7448_1_pin14), .dp(1'b0));

  // Notes on the sheet:
  //   Complemento de 2
  //   //QUESTÃO 2 - somador/sutrator de 4 bits
  //   2ª entrada
  //   1ª entrada
endmodule
