// Digital circuit questão 3. prática 2.dig as structural Verilog
module \questão_3__prática_2  (
  input  P1,
  input  P2,
  input  P3,
  input  P4,
  input  P5,
  input  P6,
  input  P7,
  input  P8,
  input  P9,
  input  P10,
  input  P11,
  input  P12,
  input  Q1,
  input  Q2,
  input  Q3,
  input  Q4,
  input  Q5,
  input  Q6,
  input  Q7,
  input  Q8,
  input  Q9,
  input  Q10,
  input  Q11,
  input  Q12
);

  wire _74688_1_pin19, _74688_2_pin19;

  _74688 _74688_1 (
    .pin1(1'b0), .pin2(P1), .pin3(Q1), .pin4(P2), .pin5(Q2), .pin6(P3), .pin7(Q3), .pin8(P4), .pin9(Q4),
    .pin10(1'b0), .pin11(P5), .pin12(Q5), .pin13(P6), .pin14(Q6), .pin15(P7), .pin16(Q7), .pin17(P8),
    .pin18(Q8), .pin19(_74688_1_pin19), .pin20(1'b1));
  _74688 _74688_2 (
    .pin1(_74688_1_pin19), .pin2(P12), .pin3(Q12), .pin4(P11), .pin5(Q11), .pin6(P10), .pin7(Q10), .pin8(P9),
    .pin9(Q9), .pin10(1'b0), .pin11(1'b0), .pin12(1'b0), .pin13(1'b0), .pin14(1'b0), .pin15(1'b0),
    .pin16(1'b0), .pin17(1'b0), .pin18(1'b0), .pin19(_74688_2_pin19), .pin20(1'b1));
  LED led_1 (.in(_74688_2_pin19));

  // Notes on the sheet:
  //   // Questão 3 - Circuito comparador de 12 bits
  //   0 - Iguais 
  //   1 - Diferentes
  //   Casos de Testes
  //   ......|................ P...............|...............  Q...............|...... S ....|
  //   1º..|....000000000000.....|....000000000000.....|........0......|
  //   2º..|....111111111111.....|.....111111111111....|........0......|
  //   3º..|....010101010101.....|.....010101010101....|........0......|
  //   4º..|....100000100000.....|.....010000100000....|........1......|
  //   5º..|....111111111111.....|.....000000000000....|........1......|
  //   6º..|....101010101010.....|.....010101010101....|........1......|
endmodule
