// Digital circuit quetao 2 diferente.dig as structural Verilog
module quetao_2_diferente (
  input  A1,
  input  A2,
  input  A3,
  input  A4,
  input  B1,
  input  B2,
  input  B3,
  input  B4,
  input  in_17,
  output out_9,
  output out_10,
  output out_11,
  output out_12,
  output out_13,
  output out_14,
  output out_15,
  output out_16,
  output OVERFLOW,
  output OVERFLOW_2,
  output OVERFLOW_3
);

  wire _7448_1_pin9, _7448_1_pin10, _7448_1_pin11, _7448_1_pin12, _7448_1_pin13, _7448_1_pin14,
       _7448_1_pin15, and_1_out, and_2_out, and_3_out, and_4_out, and_5_out, and_6_out, and_7_out, and_8_out,
       and_9_out, and_10_out, and_11_out, and_12_out, and_14_out, and_15_out, and_16_out, and_18_out,
       and_19_out, and_20_out, and_22_out, and_23_out, and_24_out, and_25_out, and_26_out, and_27_out,
       and_28_out, not_1_out, not_2_out, not_3_out, not_4_out, xor_1_out, xor_4_out, xor_6_out, xor_8_out,
       xor_9_out, xor_11_out, xor_12_out, xor_13_out, xor_14_out, xor_16_out, xor_18_out, xor_19_out;
  wire [3:0] multiplexer_1_out, xor_7_out, xor_10_out;

  xor xor_1 (xor_1_out, A1, B1);
  xor xor_2 (xor_7_out[0], xor_1_out, 1'b0);
  and and_1 (and_1_out, 1'b0, B1);
  or or_1 (out_10, and_1_out, and_2_out, and_3_out);
  and and_2 (and_2_out, 1'b0, A1);
  and and_3 (and_3_out, A1, B1);
  xor xor_3 (xor_7_out[1], xor_4_out, out_10);
  xor xor_4 (xor_4_out, A2, B2);
  and and_4 (and_4_out, out_10, B2);
  or or_2 (out_9, and_4_out, and_5_out, and_6_out);
  and and_5 (and_5_out, out_10, A2);
  and and_6 (and_6_out, A2, B2);
  xor xor_5 (xor_7_out[2], xor_6_out, out_9);
  xor xor_6 (xor_6_out, A3, B3);
  and and_7 (and_7_out, out_9, B3);
  or or_3 (out_11, and_7_out, and_8_out, and_9_out);
  and and_8 (and_8_out, out_9, A3);
  and and_9 (and_9_out, A3, B3);
  xor xor_7 (xor_7_out[3], xor_8_out, out_11);
  xor xor_8 (xor_8_out, A4, B4);
  and and_10 (and_10_out, out_11, B4);
  or or_4 (OVERFLOW_3, and_10_out, and_11_out, and_12_out);
  and and_11 (and_11_out, out_11, A4);
  and and_12 (and_12_out, A4, B4);
  Multiplexer #(.Bits(4)) multiplexer_1 (.sel(B4), .in_0(xor_7_out), .in_1(xor_10_out), .out(multiplexer_1_out));
  xor xor_9 (xor_9_out, not_1_out, 1'b1);
  not not_1 (not_1_out, B1);
  not not_2 (not_2_out, B2);
  not not_3 (not_3_out, B3);
  not not_4 (not_4_out, B4);
  xor xor_10 (xor_10_out[0], xor_11_out, 1'b0);
  xor xor_11 (xor_11_out, A1, xor_9_out);
  and and_13 (out_12, 1'b1, not_1_out);
  and and_14 (and_14_out, 1'b0, A1);
  or or_5 (out_14, and_14_out, and_15_out, and_16_out);
  and and_15 (and_15_out, 1'b0, xor_9_out);
  xor xor_12 (xor_12_out, out_12, not_2_out);
  _7448 _7448_1 (
    .pin1(multiplexer_1_out[1]), .pin2(multiplexer_1_out[2]), .pin3(in_17), .pin4(in_17), .pin5(in_17),
    .pin6(multiplexer_1_out[3]), .pin7(multiplexer_1_out[0]), .pin8(1'b0), .pin9(_7448_1_pin9),
    .pin10(_7448_1_pin10), .pin11(_7448_1_pin11), .pin12(_7448_1_pin12), .pin13(_7448_1_pin13),
    .pin14(_7448_1_pin14), .pin15(_7448_1_pin15), .pin16(1'b1));
  and and_16 (and_16_out, xor_9_out, A1);
  and and_17 (out_13, out_12, not_2_out);
  xor xor_13 (xor_13_out, A2, xor_12_out);
  xor xor_14 (xor_14_out, out_13, not_3_out);
  xor xor_15 (xor_10_out[1], xor_13_out, out_14);
  and and_18 (and_18_out, out_13, not_3_out);
  Seven_Seg seven_seg_1 (
    .a(_7448_1_pin13), .b(_7448_1_pin12), .c(_7448_1_pin11), .d(_7448_1_pin10), .e(_7448_1_pin9),
    .f(_7448_1_pin15), .g(_7448_1_pin14), .dp(1'b0));
  and and_19 (and_19_out, out_14, A2);
  xor xor_16 (xor_16_out, and_18_out, not_4_out);
  or or_6 (out_15, and_19_out, and_20_out, and_22_out);
  and and_20 (and_20_out, out_14, xor_12_out);
  and and_21 (OVERFLOW_2, and_18_out, not_4_out);
  and and_22 (and_22_out, xor_12_out, A2);
  xor xor_17 (xor_10_out[2], xor_18_out, out_15);
  xor xor_18 (xor_18_out, A3, xor_14_out);
  and and_23 (and_23_out, out_15, A3);
  or or_7 (out_16, and_23_out, and_24_out, and_25_out);
  and and_24 (and_24_out, out_15, xor_14_out);
  and and_25 (and_25_out, xor_14_out, A3);
  xor xor_19 (xor_19_out, A4, xor_16_out);
  xor xor_20 (xor_10_out[3], xor_19_out, out_16);
  and and_26 (and_26_out, out_16, A4);
  or or_8 (OVERFLOW, and_26_out, and_27_out, and_28_out);
  and and_27 (and_27_out, out_16, xor_16_out);
  and and_28 (and_28_out, xor_16_out, A4);

  // Notes on the sheet:
  //   Soma
  //   1ª ENTRADA
  //   2ª ENTRADA
  //   COMPLEMENTO DE 2
  //   Subtração
endmodule
