// Digital circuit subtrator de 3 bits.dig as structural Verilog
module subtrator_de_3_bits (
  input  A0,
  input  B0,
  input  B1,
  input  B2,
  input  A1,
  input  A2
);

  wire and_1_out, and_2_out, and_3_out, and_4_out, and_5_out, and_6_out, and_7_out, and_8_out, and_9_out,
       not_1_out, not_2_out, not_3_out, not_4_out, not_5_out, not_6_out, or_1_out, or_2_out, or_3_out,
       xor_1_out, xor_2_out, xor_3_out, xor_4_out, xor_5_out, xor_6_out;

  not not_1 (not_1_out, A0);
  not not_2 (not_2_out, A0);
  xor xor_1 (xor_1_out, B0, A0);
  and and_1 (and_1_out, not_1_out, 1'b0);
  and and_2 (and_2_out, not_2_out, B0);
  and and_3 (and_3_out, B0, 1'b0);
  xor xor_2 (xor_2_out, xor_1_out, 1'b0);
  or or_1 (or_1_out, and_1_out, and_2_out, and_3_out);
  LED S0 (.in(xor_2_out));
  LED cout (.in(or_1_out));
  xor xor_3 (xor_3_out, A1, B1);
  xor xor_4 (xor_4_out, xor_3_out, or_1_out);
  and and_4 (and_4_out, not_3_out, or_1_out);
  not not_3 (not_3_out, A1);
  and and_5 (and_5_out, not_4_out, B1);
  not not_4 (not_4_out, A1);
  and and_6 (and_6_out, B1, or_1_out);
  LED S1 (.in(xor_4_out));
  or or_2 (or_2_out, and_4_out, and_5_out, and_6_out);
  LED led_1 (.in(or_2_out));
  xor xor_5 (xor_5_out, A2, B2);
  xor xor_6 (xor_6_out, xor_5_out, or_2_out);
  not not_5 (not_5_out, A2);
  not not_6 (not_6_out, A2);
  and and_7 (and_7_out, not_5_out, or_2_out);
  and and_8 (and_8_out, not_6_out, B2);
  and and_9 (and_9_out, or_2_out, B2);
  LED S2 (.in(xor_6_out));
  or or_3 (or_3_out, and_7_out, and_8_out, and_9_out);
  LED led_2 (.in(or_3_out));
endmodule
