// Digital circuit ula pratica 22-6-23.dig as structural Verilog
module ula_pratica_22_6_23 (
  input  [3:0] A,
  input  [3:0] S,
  input  in_3,
  input  in_4,
  input  [3:0] B
);

  wire Cout, f0, f1, f2, f3, na0, na1, na2, na3, nb0, nb1, nb2, nb3, undriven, undriven_2, undriven_3;
  wire [3:0] not_1_out;

  Seven_Seg_Hex seven_seg_hex_1 (.d({3'b000, Cout}), .dp(1'b0));
  Seven_Seg_Hex seven_seg_hex_2 (.d(not_1_out), .dp(1'b0));
  assign not_1_out = ~{f3, f2, f1, f0};  // Not not_1, 4 bits wide
  _74181 _74181_1 (
    .pin1(nb0), .pin2(na0), .pin3(S[3]), .pin4(S[2]), .pin5(S[1]), .pin6(S[0]), .pin7(in_3), .pin8(in_4),
    .pin9(f0), .pin10(f1), .pin11(f2), .pin12(1'b0));  // open: pin13, pin14, pin15, pin16, pin17, pin18, pin19, pin20, pin21, pin22, pin23, pin24
  LED led_1 (.in(undriven));
  LED led_2 (.in(undriven_2));
  LED led_3 (.in(undriven_3));
  Seven_Seg_Hex seven_seg_hex_3 (.d(A), .dp(1'b0));
  Seven_Seg_Hex seven_seg_hex_4 (.d(B), .dp(1'b0));
  assign {na3, na2, na1, na0} = ~A;  // Not not_2, 4 bits wide
  assign {nb3, nb2, nb1, nb0} = ~B;  // Not not_3, 4 bits wide

  // Other names for the same wires on the sheet: Cout3[0] = Cout
endmodule
